// Logisim project Lab Week 8.circ as structural Verilog: 9 circuits, main circuit main
module main (
  input  in_1
);

  wire Manual_Clock, n4_bit_counter_1_bit_2, n4_bit_counter_1_bit_3, n4_bit_counter_1_bit_4,
       n4_bit_counter_1_co, or_1_out, or_2_out, or_3_out, or_5_out;
  wire [7:0] adder_1_out, multiplexer_1_out, multiplier_1_out, not_1_out, not_2_out, register_1_q, rom_1_data;
  wire [14:0] _0_out;

  Button _1 (.out(_0_out[1]));
  Button button (.out(_0_out[10]));
  Button _4 (.out(_0_out[4]));
  Button button_2 (.out(_0_out[11]));
  Button button_3 (.out(_0_out[12]));
  Button _7 (.out(_0_out[7]));
  Button _0 (.out(_0_out[0]));
  Button E (.out(_0_out[13]));
  Button _3 (.out(_0_out[3]));
  Button _2 (.out(_0_out[2]));
  Button _5 (.out(_0_out[5]));
  Button _6 (.out(_0_out[6]));
  Button _9 (.out(_0_out[9]));
  Button _8 (.out(_0_out[8]));
  Button CL (.out(_0_out[14]));
  or or_1 (or_1_out, in_1, or_3_out);
  or or_2 (or_2_out, _0_out[0], _0_out[1], _0_out[2], _0_out[3], _0_out[4], _0_out[6], _0_out[7], _0_out[8], _0_out[9]);
  or or_3 (or_3_out, _0_out[10], _0_out[11], _0_out[12], _0_out[13], _0_out[14]);
  _4_Bit_Counter u_4_bit_counter_1 (
    .Increment(or_2_out), .RST(or_1_out), .CI(1'b0), .Bit_2(n4_bit_counter_1_bit_2),
    .Bit_3(n4_bit_counter_1_bit_3), .Bit_4(n4_bit_counter_1_bit_4), .CO(n4_bit_counter_1_co));  // open: Bit_1
  or or_4 (Manual_Clock, or_2_out, or_3_out);
  Multiplier multiplier_1 (.a(register_1_q), .b(8'hfa), .out(multiplier_1_out));  // open: cin, cout
  or or_5 (or_5_out, n4_bit_counter_1_bit_3, n4_bit_counter_1_bit_2, n4_bit_counter_1_bit_4, n4_bit_counter_1_co);
  ROM #(.addrWidth(15)) rom_1 (.addr(_0_out), .data(rom_1_data));  // open: sel
  assign not_1_out = ~rom_1_data;  // NOT_Gate not_1, 8 bits wide
  Multiplexer #(.width(8), .enable("false")) multiplexer_1 (
    .in0(register_1_q), .in1(adder_1_out), .out(multiplexer_1_out), .sel(or_5_out));
  Adder adder_1 (.a(multiplier_1_out), .b(register_1_q), .out(adder_1_out));  // open: cin, cout
  assign not_2_out = ~not_1_out;  // NOT_Gate not_2, 8 bits wide
  Register #(.trigger("high")) register_1 (.D(not_2_out), .Q(register_1_q), .clk(Manual_Clock));  // open: en, clr
  Register #(.trigger("high")) register_2 (.D(multiplexer_1_out), .clk(Manual_Clock));  // open: en, Q, clr

  // Notes on the sheet:
  //   contents of rom_1 (hex, n*v repeats v):
  //   0 0 1 0 2 0 0 0 3 7*0 4 15*0 5 31*0 6 63*0 7 127*0 8 255*0 9 511*0 a 1023*0 b 2047*0 c 4095*0 d
  //   8191*0 e
endmodule

module D_Level_Latch (
  input  D,
  input  Clock,
  output Q,
  output NOT_Q
);

  wire nand_1_out, nand_2_out, not_1_out;

  not not_1 (not_1_out, D);
  nand nand_1 (nand_1_out, D, Clock);
  nand nand_2 (nand_2_out, Clock, not_1_out);
  nand nand_3 (Q, nand_1_out, NOT_Q);
  nand nand_4 (NOT_Q, Q, nand_2_out);
endmodule

module _2_Phase_Clock (
  output phi_1,
  output phi_2
);

  wire clock_1_out, nand_1_out, nand_2_out, not_1_out, not_2_out, not_3_out;

  Clock clock_1 (.out(clock_1_out));
  not not_1 (not_1_out, clock_1_out);
  not not_2 (not_2_out, nand_1_out);
  nand nand_1 (nand_1_out, not_1_out, phi_2);
  nand nand_2 (nand_2_out, phi_1, clock_1_out);
  not not_3 (not_3_out, nand_2_out);
  not not_4 (phi_1, not_2_out);
  not not_5 (phi_2, not_3_out);
endmodule

module Attempt_1 (
);

  wire _0_out, _1_out, _2_out, _3_out, _4_out, _5_out, _6_out, _7_out, _8_out, _9_out, button_out;

  Button _1 (.out(_1_out));
  Button _4 (.out(_4_out));
  Button _7 (.out(_7_out));
  Button _0 (.out(_0_out));
  Button button (.out(button_out));
  Button _3 (.out(_3_out));
  Button _2 (.out(_2_out));
  Button _5 (.out(_5_out));
  Button _6 (.out(_6_out));
  Button _8 (.out(_8_out));
  Button _9 (.out(_9_out));
  Demultiplexer #(.select(3), .width(2)) demultiplexer_1 ();  // open: out0, out1, out2, out3, out4, out5, out6, out7, in, sel, en
  Multiplexer #(.select(3)) multiplexer_1 ();  // open: in0, in1, in2, in3, in4, in5, in6, in7, out, sel, en
endmodule

module Full_Adder (
  input  CI,
  input  X,
  input  Y,
  output CO,
  output R
);

  wire and_1_out, and_2_out, xor_1_out;

  and and_1 (and_1_out, X, Y);
  xor xor_1 (xor_1_out, X, Y);
  and and_2 (and_2_out, xor_1_out, CI);
  or or_1 (CO, and_2_out, and_1_out);
  xor xor_2 (R, CI, xor_1_out);
endmodule

module _4_Bit_Ripple_Adder (
  input  CI,
  input  X,
  input  Y,
  input  X2,
  input  Y2,
  input  X3,
  input  Y3,
  input  X4,
  input  Y4,
  output R0,
  output R1,
  output R2,
  output R3,
  output Final_CO
);

  wire full_adder_1_co, full_adder_2_co, full_adder_3_co;

  Full_Adder full_adder_1 (.CI(CI), .X(X), .Y(Y), .CO(full_adder_1_co), .R(R0));
  Full_Adder full_adder_2 (.CI(full_adder_1_co), .X(X2), .Y(Y2), .CO(full_adder_2_co), .R(R1));
  Full_Adder full_adder_3 (.CI(full_adder_2_co), .X(X3), .Y(Y3), .CO(full_adder_3_co), .R(R2));
  Full_Adder full_adder_4 (.CI(full_adder_3_co), .X(X4), .Y(Y4), .CO(Final_CO), .R(R3));
endmodule

module _4_Bit_Counter (
  input  Increment,
  input  RST,
  input  CI,
  output Bit_1,
  output Bit_2,
  output Bit_3,
  output Bit_4,
  output CO
);

  wire and_1_out, and_2_out, and_3_out, and_4_out, d_level_latch_1_q, d_level_latch_2_q, d_level_latch_3_q,
       d_level_latch_4_q, d_level_latch_5_q, d_level_latch_6_q, d_level_latch_7_q, d_level_latch_8_q,
       full_adder_1_co, full_adder_2_co, full_adder_3_co, not_1_out, not_2_out;

  not not_1 (not_1_out, Increment);
  not not_2 (not_2_out, RST);
  D_Level_Latch d_level_latch_1 (.D(d_level_latch_2_q), .Clock(not_1_out), .Q(d_level_latch_1_q));  // open: NOT_Q
  D_Level_Latch d_level_latch_2 (.D(and_1_out), .Clock(Increment), .Q(d_level_latch_2_q));  // open: NOT_Q
  Full_Adder full_adder_1 (.CI(CI), .X(d_level_latch_1_q), .Y(1'b1), .CO(full_adder_1_co), .R(Bit_1));
  and and_1 (and_1_out, not_2_out, Bit_1);
  D_Level_Latch d_level_latch_3 (.D(d_level_latch_4_q), .Clock(not_1_out), .Q(d_level_latch_3_q));  // open: NOT_Q
  D_Level_Latch d_level_latch_4 (.D(and_2_out), .Clock(Increment), .Q(d_level_latch_4_q));  // open: NOT_Q
  and and_2 (and_2_out, not_2_out, Bit_2);
  Full_Adder full_adder_2 (.CI(full_adder_1_co), .X(d_level_latch_3_q), .Y(1'b0), .CO(full_adder_2_co), .R(Bit_2));
  D_Level_Latch d_level_latch_5 (.D(d_level_latch_6_q), .Clock(not_1_out), .Q(d_level_latch_5_q));  // open: NOT_Q
  D_Level_Latch d_level_latch_6 (.D(and_3_out), .Clock(Increment), .Q(d_level_latch_6_q));  // open: NOT_Q
  and and_3 (and_3_out, not_2_out, Bit_3);
  Full_Adder full_adder_3 (.CI(full_adder_2_co), .X(d_level_latch_5_q), .Y(1'b0), .CO(full_adder_3_co), .R(Bit_3));
  D_Level_Latch d_level_latch_7 (.D(d_level_latch_8_q), .Clock(not_1_out), .Q(d_level_latch_7_q));  // open: NOT_Q
  D_Level_Latch d_level_latch_8 (.D(and_4_out), .Clock(Increment), .Q(d_level_latch_8_q));  // open: NOT_Q
  and and_4 (and_4_out, not_2_out, Bit_4);
  Full_Adder full_adder_4 (.CI(full_adder_3_co), .X(d_level_latch_7_q), .Y(1'b0), .CO(CO), .R(Bit_4));

  // Notes on the sheet:
  //   Rst
  //   Inital Carry In
endmodule

module Attempt_2 (
  input  [3:0] in_1,
  input  [3:0] Enter,
  input  in_3,
  output [3:0] out_4
);

  wire [3:0] demultiplexer_1_out0, demultiplexer_1_out1;

  Demultiplexer #(.width(4)) demultiplexer_1 (
    .out0(demultiplexer_1_out0), .out1(demultiplexer_1_out1), .in(in_1), .en(Enter[0]));  // open: sel
  Register #(.width(4)) register_1 (.D(demultiplexer_1_out0), .Q(out_4), .clk(in_3));  // open: en, clr
  Register #(.width(4)) register_2 (.D(demultiplexer_1_out1));  // open: en, Q, clk, clr
  // Pins of 1 and 4 bits meet at Enter
endmodule

module Attempt_3 (
  input  Increment,
  input  RST,
  output [3:0] out_3,
  output [3:0] out_4,
  output [3:0] out_5
);

  wire or_1_out, undriven;
  wire [3:0] _0_out, demultiplexer_1_out1, demultiplexer_2_out2, n4_bit_counter_1_bit_1;

  Button _1 (.out(_0_out[1]));
  Button _2 (.out(_0_out[2]));
  Button _3 (.out(_0_out[3]));
  Multiplexer multiplexer_1 ();  // open: in0, in1, out, sel, en
  Button _0 (.out(_0_out[0]));
  or or_1 (or_1_out, _0_out[1], _0_out[2], _0_out[3]);
  _4_Bit_Counter u_4_bit_counter_1 (
    .Increment(Increment), .RST(RST), .CI(1'b0), .Bit_1(n4_bit_counter_1_bit_1[0]),
    .Bit_2(n4_bit_counter_1_bit_1[1]), .Bit_3(n4_bit_counter_1_bit_1[2]), .Bit_4(n4_bit_counter_1_bit_1[3]));  // open: CO
  Register #(.width(4)) X (.D(_0_out), .en(undriven), .Q(out_3), .clk(or_1_out));  // open: clr
  Demultiplexer #(.select(4), .width(4), .enable("false")) demultiplexer_1 (
    .out1(demultiplexer_1_out1), .in(out_3), .sel(n4_bit_counter_1_bit_1));  // open: out0, out2, out3, out4, out5, out6, out7, out8, out9, out10, out11, out12, out13, out14, out15
  Register #(.width(4), .trigger("high")) Y (
    .D(demultiplexer_1_out1), .en(undriven), .Q(out_4), .clk(or_1_out));  // open: clr
  Demultiplexer #(.select(4), .width(4), .enable("false")) demultiplexer_2 (
    .out2(demultiplexer_2_out2), .sel(n4_bit_counter_1_bit_1));  // open: out0, out1, out3, out4, out5, out6, out7, out8, out9, out10, out11, out12, out13, out14, out15, in
  Register #(.width(4), .trigger("high")) Z (
    .D(demultiplexer_2_out2), .en(undriven), .Q(out_5), .clk(or_1_out));  // open: clr
endmodule
