// Logisim project lab-4.q.circ as structural Verilog
module Not_gate (
  input  in_1,
  output out_2
);

  Transistor transistor_1 (.in(1'b1), .out(out_2), .gate(in_1));
  Transistor #(.\type ("n")) transistor_2 (.in(1'b0), .out(out_2), .gate(in_1));
endmodule

module Nor_Gate (
  input  in_1,
  input  in_2,
  output out_3
);

  wire transistor_1_out;

  Transistor transistor_1 (.in(1'b1), .out(transistor_1_out), .gate(in_1));
  Transistor transistor_2 (.in(transistor_1_out), .out(out_3), .gate(in_2));
  Transistor #(.\type ("n")) transistor_3 (.in(1'b0), .out(out_3), .gate(in_1));
  Transistor #(.\type ("n")) transistor_4 (.in(1'b0), .out(out_3), .gate(in_2));
endmodule

module Nand (
  input  in_1,
  input  in_2,
  output out_3
);

  wire transistor_3_out;

  Transistor transistor_1 (.in(1'b1), .out(out_3), .gate(in_2));
  Transistor #(.\type ("n")) transistor_2 (.in(transistor_3_out), .out(out_3), .gate(in_1));
  Transistor #(.\type ("n")) transistor_3 (.in(1'b0), .out(transistor_3_out), .gate(in_2));
  Transistor transistor_4 (.in(1'b1), .out(out_3), .gate(in_1));
endmodule

module Universality (
  input  Inputs_X_and_Y,
  input  in_2,
  input  in_3,
  input  in_4,
  output Output,
  output Output_2
);

  wire nand_1_out_3, nor_1_out_3;

  Nor_Gate nor_1 (.in_1(Inputs_X_and_Y), .in_2(in_2), .out_3(nor_1_out_3));
  Nand nand_1 (.in_1(in_3), .in_2(in_4), .out_3(nand_1_out_3));
  Not_gate not_gate_1 (.out_2(Output), .in_1(nor_1_out_3));
  Not_gate not_gate_2 (.out_2(Output_2), .in_1(nand_1_out_3));

  // Notes on the sheet:
  //   NOR
  //   NAND
  //   NOT
  //   NOT
endmodule

module _3_Input_Nand (
  input  in_1,
  input  in_2,
  input  in_3,
  output out_4
);

  wire transistor_3_out, transistor_5_out;

  Transistor transistor_1 (.in(1'b1), .out(out_4), .gate(in_2));
  Transistor #(.\type ("n")) transistor_2 (.in(transistor_3_out), .out(out_4), .gate(in_1));
  Transistor #(.\type ("n")) transistor_3 (.in(transistor_5_out), .out(transistor_3_out), .gate(in_2));
  Transistor transistor_4 (.in(1'b1), .out(out_4), .gate(in_1));
  Transistor #(.\type ("n")) transistor_5 (.in(1'b0), .out(transistor_5_out), .gate(in_3));
  Transistor transistor_6 (.in(1'b1), .out(out_4), .gate(in_3));
endmodule
