// Logisim project lab-5.q.circ as structural Verilog
module Multiplexer (
  input  in_1,
  input  in_2,
  input  in_3,
  output out_4
);

  wire and_1_out, and_2_out, not_1_out;

  not not_1 (not_1_out, in_3);
  and and_1 (and_1_out, in_1, not_1_out);
  and and_2 (and_2_out, in_2, in_3);
  or or_1 (out_4, and_1_out, and_2_out);
endmodule

module Half_adder (
  input  in_1,
  input  in_2,
  output out_3
);

  // AND_Gate and_1 has open pins: in0=in_1, in1=in_2, out=open
  xor xor_1 (out_3, in_1, in_2);
endmodule

module Full_adder (
  input  in_1,
  input  in_2,
  input  in_3,
  output out_4,
  output out_5
);

  wire and_1_out, and_2_out, xor_1_out;

  and and_1 (and_1_out, in_2, in_3);
  xor xor_1 (xor_1_out, in_2, in_3);
  xor xor_2 (out_5, in_1, xor_1_out);
  and and_2 (and_2_out, xor_1_out, in_1);
  or or_1 (out_4, and_2_out, and_1_out);

  // Notes on the sheet:
  //   Output
  //   Carry out
endmodule

module _4_Bit_Ripple_Adder (
  input  in_1,
  input  in_2,
  input  in_3,
  input  in_4,
  input  in_5,
  input  in_6,
  input  in_7,
  input  in_8,
  input  in_9,
  output out_10,
  output out_11,
  output out_12,
  output out_13,
  output out_14
);

  wire full_adder_1_out_4, full_adder_2_out_4, full_adder_3_out_4;

  Full_adder full_adder_1 (.in_1(in_1), .in_2(in_2), .in_3(in_3), .out_4(full_adder_1_out_4), .out_5(out_10));
  Full_adder full_adder_2 (
    .in_1(full_adder_1_out_4), .in_2(in_4), .in_3(in_5), .out_4(full_adder_2_out_4), .out_5(out_11));
  Full_adder full_adder_3 (
    .in_1(full_adder_2_out_4), .in_2(in_6), .in_3(in_7), .out_4(full_adder_3_out_4), .out_5(out_12));
  Full_adder full_adder_4 (.in_1(full_adder_3_out_4), .in_2(in_8), .in_3(in_9), .out_4(out_14), .out_5(out_13));
endmodule

module Full_Subtractor (
  input  in_1,
  input  in_2,
  input  in_3,
  output Borrow_Out,
  output Difference
);

  wire and_1_out, and_2_out, not_1_out, not_2_out, xor_1_out;

  xor xor_1 (xor_1_out, in_1, in_2);
  not not_1 (not_1_out, in_1);
  and and_1 (and_1_out, not_1_out, in_2);
  xor xor_2 (Difference, in_3, xor_1_out);
  not not_2 (not_2_out, xor_1_out);
  and and_2 (and_2_out, in_3, not_2_out);
  or or_1 (Borrow_Out, and_2_out, and_1_out);
endmodule

module _4_Bit_Ripple_Subtractor (
  input  in_1,
  input  in_2,
  input  in_3,
  input  in_4,
  input  in_5,
  input  in_6,
  input  in_7,
  input  in_8,
  input  in_9,
  output out_10,
  output out_11,
  output out_12,
  output out_13,
  output out_14
);

  wire full_subtractor_1_borrow_out, full_subtractor_2_borrow_out, full_subtractor_3_borrow_out;

  Full_Subtractor full_subtractor_1 (
    .in_1(in_1), .in_2(in_2), .in_3(in_3), .Borrow_Out(full_subtractor_1_borrow_out), .Difference(out_12));
  Full_Subtractor full_subtractor_2 (
    .in_1(full_subtractor_1_borrow_out), .in_2(in_6), .in_3(in_5), .Borrow_Out(full_subtractor_2_borrow_out),
    .Difference(out_13));
  Full_Subtractor full_subtractor_3 (
    .in_1(full_subtractor_2_borrow_out), .in_2(in_4), .in_3(in_7), .Borrow_Out(full_subtractor_3_borrow_out),
    .Difference(out_14));
  Full_Subtractor full_subtractor_4 (
    .in_1(full_subtractor_3_borrow_out), .in_2(in_8), .in_3(in_9), .Borrow_Out(out_10), .Difference(out_11));

  // Notes on the sheet:
  //   Difference
  //   Borrow Out
endmodule
