// Logisim project lab-6.q.circ as structural Verilog: 8 circuits, main circuit main
module main (
  input  in_1
);

  wire clk_2phase_1_phi_1, clk_2phase_1_phi_2, d_nand_latch_1_q, d_nand_latch_2_q, d_nand_latch_3_q,
       d_nand_latch_4_q, d_nand_latch_5_q, d_nand_latch_6_q, omega_1_aa, omega_1_ag, omega_1_ar, omega_1_ma,
       omega_1_mg, omega_1_mr, primes_1_out_5, primes_1_out_6, primes_1_out_7;

  clk_2phase clk_2phase_1 (.phi_1(clk_2phase_1_phi_1), .phi_2(clk_2phase_1_phi_2));
  D_NAND_Latch d_nand_latch_1 (
    .in_1(d_nand_latch_2_q), .in_2(clk_2phase_1_phi_2), .Q(d_nand_latch_1_q));  // open: out_4
  D_NAND_Latch d_nand_latch_2 (.in_1(primes_1_out_5), .in_2(clk_2phase_1_phi_1), .Q(d_nand_latch_2_q));  // open: out_4
  Primes primes_1 (
    .in_1(d_nand_latch_1_q), .in_2(d_nand_latch_3_q), .Q2(d_nand_latch_5_q), .Reset(in_1),
    .out_5(primes_1_out_5), .out_6(primes_1_out_6), .out_7(primes_1_out_7));
  D_NAND_Latch d_nand_latch_3 (
    .in_1(d_nand_latch_4_q), .in_2(clk_2phase_1_phi_2), .Q(d_nand_latch_3_q));  // open: out_4
  D_NAND_Latch d_nand_latch_4 (.in_1(primes_1_out_6), .in_2(clk_2phase_1_phi_1), .Q(d_nand_latch_4_q));  // open: out_4
  Omega omega_1 (
    .in_1(d_nand_latch_1_q), .in_2(d_nand_latch_3_q), .in_3(d_nand_latch_5_q), .Mg(omega_1_mg),
    .Ma(omega_1_ma), .Mr(omega_1_mr), .Ag(omega_1_ag), .Aa(omega_1_aa), .Ar(omega_1_ar));
  D_NAND_Latch d_nand_latch_5 (
    .in_1(d_nand_latch_6_q), .in_2(clk_2phase_1_phi_2), .Q(d_nand_latch_5_q));  // open: out_4
  D_NAND_Latch d_nand_latch_6 (.in_1(primes_1_out_7), .in_2(clk_2phase_1_phi_1), .Q(d_nand_latch_6_q));  // open: out_4
  LED led_1 (.in(omega_1_mg));
  LED led_2 (.in(omega_1_ma));
  LED led_3 (.in(omega_1_mr));
  LED led_4 (.in(omega_1_ag));
  LED led_5 (.in(omega_1_aa));
  LED led_6 (.in(omega_1_ar));

  // Notes on the sheet:
  //   Reset
  //   Main
  //   Access
endmodule

module clk_2phase (
  output phi_1,
  output phi_2
);

  wire clock_1_out, nand_1_out, nand_2_out, not_1_out, not_2_out, not_3_out;

  Clock clock_1 (.out(clock_1_out));
  not not_1 (not_1_out, clock_1_out);
  not not_2 (not_2_out, nand_1_out);
  nand nand_1 (nand_1_out, not_1_out, phi_2);
  nand nand_2 (nand_2_out, phi_1, clock_1_out);
  not not_3 (not_3_out, nand_2_out);
  not not_4 (phi_1, not_2_out);
  not not_5 (phi_2, not_3_out);
endmodule

module Failure (
  input  in_1,
  input  R
);

  wire nand_1_out, nand_2_out, nand_3_out, nand_4_out, nand_5_out, nand_6_out, not_1_out, undriven;

  nand nand_1 (nand_1_out, in_1, in_1);
  not not_1 (not_1_out, undriven);
  nand nand_2 (nand_2_out, R, R);
  nand nand_3 (nand_3_out, undriven, undriven);
  nand nand_4 (nand_4_out, not_1_out, not_1_out);
  nand nand_5 (nand_5_out, nand_1_out, nand_3_out);
  nand nand_6 (nand_6_out, nand_4_out, nand_2_out);
  // NAND_Gate nand_7 has open pins: in0=nand_5_out, in1=nand_5_out, out=open
  // NAND_Gate nand_8 has open pins: in0=nand_6_out, in1=nand_6_out, out=open

  // Notes on the sheet:
  //   S
  //   Q
endmodule

module Full_Adder (
  input  in_1,
  input  in_2,
  input  in_3,
  output out_4,
  output out_5
);

  wire and_1_out, and_2_out, xor_1_out;

  and and_1 (and_1_out, in_2, in_3);
  xor xor_1 (xor_1_out, in_2, in_3);
  xor xor_2 (out_5, in_1, xor_1_out);
  and and_2 (and_2_out, xor_1_out, in_1);
  or or_1 (out_4, and_2_out, and_1_out);

  // Notes on the sheet:
  //   Carry out
endmodule

module D_NAND_Latch (
  input  in_1,
  input  in_2,
  output Q,
  output out_4
);

  wire nand_1_out, nand_2_out, not_1_out;

  not not_1 (not_1_out, in_1);
  nand nand_1 (nand_1_out, in_1, in_2);
  nand nand_2 (nand_2_out, in_2, not_1_out);
  nand nand_3 (Q, nand_1_out, out_4);
  nand nand_4 (out_4, Q, nand_2_out);

  // Notes on the sheet:
  //   Clock subbed for 2 phase
endmodule

module _4_Bit_Counter (
  input  Rst,
  input  Inital_Carry_In,
  input  in_3,
  input  in_4,
  input  in_5,
  input  in_6,
  output out_7,
  output out_8,
  output out_9,
  output out_10,
  output out_11
);

  wire and_1_out, and_2_out, and_3_out, and_4_out, clk_2phase_1_phi_1, clk_2phase_1_phi_2, d_nand_latch_1_q,
       d_nand_latch_2_q, d_nand_latch_3_q, d_nand_latch_4_q, d_nand_latch_5_q, d_nand_latch_6_q,
       d_nand_latch_7_q, d_nand_latch_8_q, full_adder_1_out_4, full_adder_2_out_4, full_adder_3_out_4,
       not_1_out;

  clk_2phase clk_2phase_1 (.phi_1(clk_2phase_1_phi_1), .phi_2(clk_2phase_1_phi_2));
  not not_1 (not_1_out, Rst);
  D_NAND_Latch d_nand_latch_1 (
    .in_1(d_nand_latch_2_q), .in_2(clk_2phase_1_phi_2), .Q(d_nand_latch_1_q));  // open: out_4
  D_NAND_Latch d_nand_latch_2 (.in_1(and_1_out), .in_2(clk_2phase_1_phi_1), .Q(d_nand_latch_2_q));  // open: out_4
  Full_Adder full_adder_1 (
    .in_1(Inital_Carry_In), .in_2(d_nand_latch_1_q), .in_3(in_6), .out_4(full_adder_1_out_4), .out_5(out_7));
  and and_1 (and_1_out, not_1_out, out_7);
  D_NAND_Latch d_nand_latch_3 (
    .in_1(d_nand_latch_4_q), .in_2(clk_2phase_1_phi_2), .Q(d_nand_latch_3_q));  // open: out_4
  D_NAND_Latch d_nand_latch_4 (.in_1(and_2_out), .in_2(clk_2phase_1_phi_1), .Q(d_nand_latch_4_q));  // open: out_4
  and and_2 (and_2_out, not_1_out, out_8);
  Full_Adder full_adder_2 (
    .in_1(full_adder_1_out_4), .in_2(d_nand_latch_3_q), .in_3(in_3), .out_4(full_adder_2_out_4), .out_5(out_8));
  D_NAND_Latch d_nand_latch_5 (
    .in_1(d_nand_latch_6_q), .in_2(clk_2phase_1_phi_2), .Q(d_nand_latch_5_q));  // open: out_4
  D_NAND_Latch d_nand_latch_6 (.in_1(and_3_out), .in_2(clk_2phase_1_phi_1), .Q(d_nand_latch_6_q));  // open: out_4
  and and_3 (and_3_out, not_1_out, out_9);
  Full_Adder full_adder_3 (
    .in_1(full_adder_2_out_4), .in_2(d_nand_latch_5_q), .in_3(in_4), .out_4(full_adder_3_out_4), .out_5(out_9));
  D_NAND_Latch d_nand_latch_7 (
    .in_1(d_nand_latch_8_q), .in_2(clk_2phase_1_phi_2), .Q(d_nand_latch_7_q));  // open: out_4
  D_NAND_Latch d_nand_latch_8 (.in_1(and_4_out), .in_2(clk_2phase_1_phi_1), .Q(d_nand_latch_8_q));  // open: out_4
  and and_4 (and_4_out, not_1_out, out_10);
  Full_Adder full_adder_4 (
    .in_1(full_adder_3_out_4), .in_2(d_nand_latch_7_q), .in_3(in_5), .out_4(out_11), .out_5(out_10));
endmodule

module Primes (
  input  in_1,
  input  in_2,
  input  Q2,
  input  Reset,
  output out_5,
  output out_6,
  output out_7
);

  wire and_1_out, and_2_out, and_3_out, and_4_out, and_5_out, and_6_out, and_7_out, and_8_out, and_9_out,
       and_10_out, and_11_out, not_1_out, not_2_out, not_3_out, not_4_out, not_5_out, not_6_out, or_1_out,
       or_2_out;

  not not_1 (not_1_out, in_1);
  not not_2 (not_2_out, in_2);
  not not_3 (not_3_out, Q2);
  not not_4 (not_4_out, Reset);
  and and_1 (and_1_out, not_1_out, not_2_out);
  and and_2 (and_2_out, not_2_out, not_3_out);
  not not_5 (not_5_out, in_1);
  not not_6 (not_6_out, not_2_out);
  and and_3 (and_3_out, not_2_out, Q2);
  and and_4 (and_4_out, not_1_out, not_3_out);
  and and_5 (and_5_out, and_1_out, not_4_out);
  and and_6 (and_6_out, and_2_out, in_1);
  and and_7 (and_7_out, not_5_out, not_6_out);
  and and_8 (and_8_out, not_1_out, and_3_out);
  and and_9 (and_9_out, in_1, in_2);
  and and_10 (and_10_out, and_7_out, not_3_out);
  and and_11 (and_11_out, and_4_out, not_4_out);
  or or_1 (or_1_out, Reset, and_8_out);
  or or_2 (or_2_out, Reset, and_6_out);
  or or_3 (out_6, or_2_out, and_10_out);
  or or_4 (out_7, or_1_out, and_9_out);
  or or_5 (out_5, and_5_out, and_11_out);

  // Notes on the sheet:
  //   Q0
  //   Q1
  //   Q prime 0
  //   Q prime 1
  //   Q prime 2
endmodule

module Omega (
  input  in_1,
  input  in_2,
  input  in_3,
  output Mg,
  output Ma,
  output Mr,
  output Ag,
  output Aa,
  output Ar
);

  wire and_1_out, and_2_out, and_3_out, and_4_out, and_5_out, and_6_out, and_9_out, and_10_out, and_12_out,
       not_1_out, not_2_out, not_3_out, not_4_out, not_5_out, or_1_out;

  not not_1 (not_1_out, in_1);
  not not_2 (not_2_out, in_2);
  not not_3 (not_3_out, in_3);
  and and_1 (and_1_out, in_3, in_2);
  and and_2 (and_2_out, not_1_out, in_3);
  and and_3 (and_3_out, not_2_out, not_3_out);
  and and_4 (and_4_out, in_1, not_2_out);
  and and_5 (and_5_out, not_3_out, in_2);
  or or_1 (or_1_out, and_3_out, and_4_out);
  and and_6 (and_6_out, not_1_out, not_2_out);
  or or_2 (Mr, in_2, and_2_out);
  not not_4 (not_4_out, in_2);
  not not_5 (not_5_out, not_3_out);
  or or_3 (Ar, or_1_out, and_1_out);
  and and_7 (Mg, and_6_out, not_3_out);
  and and_8 (Ag, in_2, in_1);
  and and_9 (and_9_out, and_5_out, not_1_out);
  and and_10 (and_10_out, not_4_out, not_5_out);
  and and_11 (Ma, not_2_out, in_1);
  or or_4 (Aa, and_9_out, and_12_out);
  and and_12 (and_12_out, not_1_out, and_10_out);

  // Notes on the sheet:
  //   Q0
  //   Q1
  //   Q2
endmodule
