// Logisim project lab-7.q.circ as structural Verilog: 8 circuits, main circuit main
module LOOP_DATA_PATH (
  input  [1:0] Q,
  input  [1:0] CLK,
  output [3:0] i,
  output CMP
);

  wire [3:0] adder_1_out, multiplexer_1_out, Q_prime;

  D_Level_Latch d_level_latch_1 (.in_1(Q_prime[0]), .in_2(CLK[0]), .Q(i[0]));  // open: out_4
  D_Level_Latch d_level_latch_2 (.in_1(Q_prime[1]), .in_2(CLK[0]), .Q(i[1]));  // open: out_4
  D_Level_Latch d_level_latch_3 (.in_1(Q_prime[2]), .in_2(CLK[0]), .Q(i[2]));  // open: out_4
  D_Level_Latch d_level_latch_4 (.in_1(Q_prime[3]), .in_2(CLK[0]), .Q(i[3]));  // open: out_4
  Adder #(.width(4)) adder_1 (.a(i), .b(4'b0001), .out(adder_1_out));  // open: cin, cout
  Comparator #(.width(4), .mode("unsigned")) comparator_1 (.a(adder_1_out), .b(4'b1000), .lt(CMP));  // open: gt, eq
  Multiplexer #(.select(2), .width(4), .enable("false")) multiplexer_1 (
    .in0(4'b0000), .in1(4'b0000), .in2(adder_1_out), .in3(i), .out(multiplexer_1_out), .sel(Q));
  D_Level_Latch d_level_latch_5 (.in_1(multiplexer_1_out[0]), .in_2(CLK[1]), .Q(Q_prime[0]));  // open: out_4
  D_Level_Latch d_level_latch_6 (.in_1(multiplexer_1_out[1]), .in_2(CLK[1]), .Q(Q_prime[1]));  // open: out_4
  D_Level_Latch d_level_latch_7 (.in_1(multiplexer_1_out[2]), .in_2(CLK[1]), .Q(Q_prime[2]));  // open: out_4
  D_Level_Latch d_level_latch_8 (.in_1(multiplexer_1_out[3]), .in_2(CLK[1]), .Q(Q_prime[3]));  // open: out_4
endmodule

module _2_Phase_Clock (
  output phi_1,
  output phi_2
);

  wire clock_1_out, nand_1_out, nand_2_out, not_1_out, not_2_out, not_3_out;

  Clock clock_1 (.out(clock_1_out));
  not not_1 (not_1_out, clock_1_out);
  not not_2 (not_2_out, nand_1_out);
  nand nand_1 (nand_1_out, not_1_out, phi_2);
  nand nand_2 (nand_2_out, phi_1, clock_1_out);
  not not_3 (not_3_out, nand_2_out);
  not not_4 (phi_1, not_2_out);
  not not_5 (phi_2, not_3_out);
endmodule

module D_Level_Latch (
  input  in_1,
  input  in_2,
  output Q,
  output out_4
);

  wire nand_1_out, nand_2_out, not_1_out;

  not not_1 (not_1_out, in_1);
  nand nand_1 (nand_1_out, in_1, in_2);
  nand nand_2 (nand_2_out, in_2, not_1_out);
  nand nand_3 (Q, nand_1_out, out_4);
  nand nand_4 (out_4, Q, nand_2_out);
endmodule

module CONTROL_PATH (
  input  req,
  input  cmp,
  input  [1:0] Q,
  output [1:0] Q_prime
);

  wire and_1_out, and_2_out, and_3_out, and_4_out, and_5_out;

  and and_1 (and_1_out, req, Q[0]);
  and and_2 (and_2_out, req, Q[1]);
  and and_3 (and_3_out, req, ~Q[0], ~Q[1]);  // AND_Gate
  and and_4 (and_4_out, Q[1], Q[0], req);
  and and_5 (and_5_out, req, ~cmp, Q[1]);  // AND_Gate
  or or_1 (Q_prime[0], and_3_out, and_4_out, and_5_out);
  or or_2 (Q_prime[1], and_1_out, and_2_out);
endmodule

module main (
  input  [7:0] in_1,
  input  [7:0] in_2,
  input  in_3
);

  wire loop_data_path_1_cmp;
  wire [1:0] control_path_1_q_prime, d_level_latch_1_q, d_level_latch_2_q, n2_phase_clock_1_phi_1;
  wire [3:0] loop_data_path_1_i;
  wire [7:0] iterative_multiplier_data_path_1_result;

  _2_Phase_Clock u_2_phase_clock_1 (.phi_1(n2_phase_clock_1_phi_1[0]), .phi_2(n2_phase_clock_1_phi_1[1]));
  ITERATIVE_MULTIPLIER_DATA_PATH iterative_multiplier_data_path_1 (
    .X(in_1), .Y(in_2), .i(loop_data_path_1_i), .Q(d_level_latch_2_q), .CLK(n2_phase_clock_1_phi_1),
    .RESULT(iterative_multiplier_data_path_1_result));
  LOOP_DATA_PATH loop_data_path_1 (
    .CLK(n2_phase_clock_1_phi_1), .i(loop_data_path_1_i), .Q(d_level_latch_2_q), .CMP(loop_data_path_1_cmp));
  D_Level_Latch d_level_latch_1 (
    .in_1(control_path_1_q_prime[0]), .in_2(n2_phase_clock_1_phi_1[1]), .Q(d_level_latch_1_q[0]));  // open: out_4
  CONTROL_PATH control_path_1 (
    .req(in_3), .cmp(loop_data_path_1_cmp), .Q(d_level_latch_2_q), .Q_prime(control_path_1_q_prime));
  D_Level_Latch d_level_latch_2 (
    .in_1(d_level_latch_1_q[0]), .in_2(n2_phase_clock_1_phi_1[0]), .Q(d_level_latch_2_q[0]));  // open: out_4
  D_Level_Latch d_level_latch_3 (
    .in_1(control_path_1_q_prime[1]), .in_2(n2_phase_clock_1_phi_1[1]), .Q(d_level_latch_1_q[1]));  // open: out_4
  D_Level_Latch d_level_latch_4 (
    .in_1(d_level_latch_1_q[1]), .in_2(n2_phase_clock_1_phi_1[0]), .Q(d_level_latch_2_q[1]));  // open: out_4
  Hex_Digit_Display hex_digit_display_1 (.value(iterative_multiplier_data_path_1_result[3:0]));  // open: dp
  Hex_Digit_Display hex_digit_display_2 (.value(iterative_multiplier_data_path_1_result[7:4]));  // open: dp
endmodule

module ITERATIVE_MULTIPLIER_DATA_PATH (
  input  [7:0] X,
  input  [7:0] Y,
  input  [1:0] Q,
  input  [3:0] i,
  input  [1:0] CLK,
  output [7:0] RESULT
);

  wire multiplexer_2_out;
  wire [7:0] adder_1_out, multiplexer_1_out, multiplexer_3_out, S4;

  Register #(.trigger("high")) register_1 (.D(RESULT), .en(CLK[1]), .Q(S4), .clk(1'b1));  // open: clr
  Adder adder_1 (.a({S4[6:0], 1'b0}), .b(X), .out(adder_1_out), .cin(1'b0));  // open: cout
  Multiplexer #(.width(8), .enable("false")) multiplexer_1 (
    .in0({S4[6:0], 1'b0}), .in1(adder_1_out), .out(multiplexer_1_out), .sel(multiplexer_2_out));
  Multiplexer #(.select(3), .enable("false")) multiplexer_2 (
    .in0(Y[7]), .in1(Y[6]), .in2(Y[5]), .in3(Y[4]), .in4(Y[3]), .in5(Y[2]), .in6(Y[1]), .in7(Y[0]),
    .out(multiplexer_2_out), .sel(i[2:0]));
  Multiplexer #(.select(2), .width(8), .enable("false")) multiplexer_3 (
    .in0({8{1'b0}}), .in1({8{1'b0}}), .in2(multiplexer_1_out), .in3(S4), .out(multiplexer_3_out), .sel(Q));
  Register #(.trigger("high")) register_2 (.D(multiplexer_3_out), .en(CLK[0]), .Q(RESULT), .clk(1'b1));  // open: clr

  // Other names for the same wires on the sheet: out[7:0] = RESULT
endmodule

module Iterative_Multiplier (
);

  // AND_Gate and_1 is placed but not wired
endmodule

module Tree (
  input  [3:0] X,
  input  [3:0] Y
);

  wire [3:0] and_1_out;
  wire [4:1] and_7_out;
  wire [5:2] and_8_out;
  wire [6:3] and_14_out;
  wire [7:0] adder_1_out, adder_2_out, adder_3_out;

  and and_1 (and_1_out[0], X[3], Y[0]);
  and and_2 (and_1_out[1], X[2], Y[0]);
  and and_3 (and_1_out[2], X[1], Y[0]);
  and and_4 (and_1_out[3], X[0], Y[0]);
  and and_5 (and_7_out[3], X[1], Y[1]);
  and and_6 (and_7_out[2], X[2], Y[1]);
  and and_7 (and_7_out[1], X[3], Y[1]);
  and and_8 (and_8_out[2], X[3], Y[2]);
  and and_9 (and_7_out[4], X[0], Y[1]);
  Adder adder_1 (.a({4'b0000, and_1_out}), .b({3'b000, and_7_out, 1'b0}), .out(adder_1_out), .cin(1'b0));  // open: cout
  and and_10 (and_8_out[5], X[0], Y[2]);
  and and_11 (and_8_out[3], X[2], Y[2]);
  and and_12 (and_8_out[4], X[1], Y[2]);
  and and_13 (and_14_out[4], X[2], Y[3]);
  and and_14 (and_14_out[3], X[3], Y[3]);
  Adder adder_2 (.a(adder_3_out), .b(adder_1_out), .out(adder_2_out), .cin(1'b0));  // open: cout
  and and_15 (and_14_out[5], X[1], Y[3]);
  and and_16 (and_14_out[6], X[0], Y[3]);
  Adder adder_3 (
    .a({1'b0, and_14_out, 3'b000}), .b({2'b00, and_8_out, 2'b00}), .out(adder_3_out), .cin(1'b0));  // open: cout
  Hex_Digit_Display hex_digit_display_1 (.value(adder_2_out[7:4]));  // open: dp
  Hex_Digit_Display hex_digit_display_2 (.value(adder_2_out[3:0]));  // open: dp
endmodule
