// Logisim project lab-9.q.circ as structural Verilog: 2 circuits, main circuit FULL ALU
module _1_Bit_ALU (
  input  Sub_En,
  input  ci,
  input  x,
  input  y,
  input  [2:0] in_5,
  input  Less,
  output Result,
  output Set,
  output Cout
);

  wire and_1_out, nor_1_out, or_1_out, xor_1_out, xor_2_out;

  xor xor_1 (xor_1_out, y, Sub_En);
  and and_1 (and_1_out, x, y);
  or or_1 (or_1_out, x, y);
  xor xor_2 (xor_2_out, x, y);
  nor nor_1 (nor_1_out, x, y);
  Adder #(.width(1)) adder_1 (.a(x), .b(xor_1_out), .out(Set), .cin(ci), .cout(Cout));
  Multiplexer #(.select(3), .enable("false")) multiplexer_1 (
    .in0(and_1_out), .in1(or_1_out), .in2(xor_2_out), .in3(nor_1_out), .in4(Set), .in5(Less), .out(Result),
    .sel(in_5));  // open: in6, in7
endmodule

module FULL_ALU (
  input  in_1,
  input  [2:0] in_2,
  input  [7:0] x,
  input  [7:0] y,
  output [7:0] out_5,
  output _0_Flag
);

  wire n1_bit_alu_1_cout, n1_bit_alu_2_cout, n1_bit_alu_3_cout, n1_bit_alu_4_cout, n1_bit_alu_5_cout,
       n1_bit_alu_6_cout, n1_bit_alu_7_cout, n1_bit_alu_8_set;

  _1_Bit_ALU u_1_bit_alu_1 (
    .x(x[0]), .y(y[0]), .in_5(in_2), .Less(n1_bit_alu_8_set), .Result(out_5[0]), .Cout(n1_bit_alu_1_cout),
    .Sub_En(in_1));  // open: Set, ci
  _1_Bit_ALU u_1_bit_alu_2 (
    .x(x[1]), .y(y[1]), .in_5(in_2), .Less(1'b0), .Result(out_5[1]), .Cout(n1_bit_alu_2_cout), .Sub_En(in_1),
    .ci(n1_bit_alu_1_cout));  // open: Set
  _1_Bit_ALU u_1_bit_alu_3 (
    .x(x[2]), .y(y[2]), .in_5(in_2), .Less(1'b0), .Result(out_5[2]), .Cout(n1_bit_alu_3_cout), .Sub_En(in_1),
    .ci(n1_bit_alu_2_cout));  // open: Set
  _1_Bit_ALU u_1_bit_alu_4 (
    .x(x[3]), .y(y[3]), .in_5(in_2), .Less(1'b0), .Result(out_5[3]), .Cout(n1_bit_alu_4_cout), .Sub_En(in_1),
    .ci(n1_bit_alu_3_cout));  // open: Set
  _1_Bit_ALU u_1_bit_alu_5 (
    .x(x[4]), .y(y[4]), .in_5(in_2), .Less(1'b0), .Result(out_5[4]), .Cout(n1_bit_alu_5_cout), .Sub_En(in_1),
    .ci(n1_bit_alu_4_cout));  // open: Set
  _1_Bit_ALU u_1_bit_alu_6 (
    .x(x[5]), .y(y[5]), .in_5(in_2), .Less(1'b0), .Result(out_5[5]), .Cout(n1_bit_alu_6_cout), .Sub_En(in_1),
    .ci(n1_bit_alu_5_cout));  // open: Set
  _1_Bit_ALU u_1_bit_alu_7 (
    .x(x[6]), .y(y[6]), .in_5(in_2), .Less(1'b0), .Result(out_5[6]), .Cout(n1_bit_alu_7_cout), .Sub_En(in_1),
    .ci(n1_bit_alu_6_cout));  // open: Set
  _1_Bit_ALU u_1_bit_alu_8 (
    .x(x[7]), .y(y[7]), .in_5(in_2), .Less(1'b0), .Result(out_5[7]), .Set(n1_bit_alu_8_set), .Sub_En(in_1),
    .ci(n1_bit_alu_7_cout));  // open: Cout
  nor nor_1 (_0_Flag, out_5[1], out_5[2], out_5[3], out_5[4], out_5[5], out_5[6], out_5[7], out_5[0]);
endmodule
